// Logisim project 4.2.circ as structural Verilog: 1 circuit, main circuit main
module main (
  input  [3:0] in_1,
  output [3:0] out_2
);

  wire not_1_out, not_2_out, not_3_out, not_4_out, or_1_out, or_2_out, or_3_out, or_4_out, or_6_out, or_7_out;

  // Probe on in_1
  not not_1 (not_1_out, in_1[3]);
  not not_2 (not_2_out, in_1[2]);
  not not_3 (not_3_out, in_1[1]);
  not not_4 (not_4_out, in_1[0]);
  or or_1 (or_1_out, in_1[3], in_1[2]);
  or or_2 (or_2_out, in_1[1], in_1[3]);
  or or_3 (or_3_out, in_1[2], in_1[1]);
  or or_4 (or_4_out, in_1[3], not_2_out, not_3_out);
  or or_5 (out_2[1], in_1[3], not_3_out);
  or or_6 (or_6_out, in_1[3], in_1[0]);
  or or_7 (or_7_out, in_1[2], in_1[1], in_1[0]);
  and and_1 (out_2[3], or_1_out, or_2_out);
  and and_2 (out_2[2], or_3_out, or_4_out);
  and and_3 (out_2[0], or_6_out, or_7_out);
  // Probe on out_2

  // Notes on the sheet:
  //   b
  //   a
  //   c
  //   d
  //   !c
  //   !b
  //   !a
  //   !d
endmodule
