// Logisim project 5.circ as structural Verilog: 1 circuit, main circuit main
module main (
  input  in_1
);

  wire and_1_out, and_2_out, and_3_out, clock_1_out, not_1_out, not_2_out, not_3_out, not_4_out, not_5_out,
       not_6_out;
  wire [3:0] D_q;

  // Probe on D_q
  Clock clock_1 (.out(clock_1_out));
  and and_1 (and_1_out, in_1, not_1_out, not_3_out, not_4_out);
  T_Flip_Flop A (.clk(clock_1_out), .T(and_1_out), .Q(D_q[3]));  // open: Qn, preset, reset, en
  and and_2 (and_2_out, in_1, not_2_out, not_5_out);
  not not_1 (not_1_out, D_q[0]);
  T_Flip_Flop B (.clk(clock_1_out), .T(and_2_out), .Q(D_q[2]));  // open: Qn, preset, reset, en
  and and_3 (and_3_out, in_1, not_6_out);
  not not_2 (not_2_out, D_q[1]);
  not not_3 (not_3_out, D_q[2]);
  not not_4 (not_4_out, D_q[1]);
  T_Flip_Flop C (.clk(clock_1_out), .T(and_3_out), .Q(D_q[1]));  // open: Qn, preset, reset, en
  not not_5 (not_5_out, D_q[0]);
  T_Flip_Flop D (.clk(clock_1_out), .T(in_1), .Q(D_q[0]));  // open: Qn, preset, reset, en
  not not_6 (not_6_out, D_q[0]);
endmodule
